# Fritzing sketch USB-Timer 3 (saved by Fritzing 0.9.6b)

parts:
  WeMos_D1_Mini1 = WeMos D1 Mini
  Q1 = MOSFET-NCHANNEL [package=to220v]
  R1 = Resistor [tolerance=±5% power=0.25 resistance=220 package=THT]
  X2 = USB Connectors [package=usb-a-s-silk-female]
  JP1 = USB_MICROB_PLUG [package=micro-b-th]
  X3 = USB Connectors [package=usb-a-s-silk-female]  # not connected
  X4 = USB Connectors [package=usb-a-s-silk-female]  # not connected
  X5 = USB Connectors [package=usb-a-s-silk-female]  # not connected
  JP2 = USB_MICROB_PLUG [package=micro-b-th]  # not connected
  JP3 = USB_MICROB_PLUG [package=micro-b-th]  # not connected
  JP4 = USB_MICROB_PLUG [package=micro-b-th]  # not connected
  Q2 = MOSFET-NCHANNEL [package=to220v]
  Q3 = MOSFET-NCHANNEL [package=to220v]
  Q4 = MOSFET-NCHANNEL [package=to220v]
  S1 = SWITCH-MOMENTARY-2 [package=tactile-pth-12mm]
  R3 = Resistor [tolerance=±5% power=0.25 resistance=220 package=THT]
  R4 = Resistor [tolerance=±5% power=0.25 resistance=220 package=THT]
  R2 = Resistor [tolerance=±5% power=0.25 resistance=220 package=THT]

nets:
  N1: WeMos_D1_Mini1.D4, S1.1
  N2: WeMos_D1_Mini1.D5, Q4.G, R4.Pin_0
  N3: WeMos_D1_Mini1.D6, Q3.G, R3.Pin_0
  N4: WeMos_D1_Mini1.D7, Q2.G, R2.Pin_0
  N5: WeMos_D1_Mini1.D8, Q1.G, R1.Pin_0
  GND: WeMos_D1_Mini1.G, Q1.S, R1.Pin_1, JP1.GND, S1.2
  N6: Q1.D, X2.GND
  N7: X2.D+, JP1.D+
  N8: X2.D-, JP1.D-
  N9: X2.VBUS, JP1.VCC
  N10: Q2.S, R2.Pin_1
  N11: Q3.S, R3.Pin_1
  N12: Q4.S, R4.Pin_1

notes:
  Device 1
  D8
  Device 2
  D7
  Device 3
  D6
  Device 4
  D5
  Wifi Reset
  D4
  Computer1
  Computer2
  Computer3
  Computer4
